# Fritzing sketch smellBot_Schematics (saved by Fritzing 0.8.7b)
circuit board: 2.77362cm x 1.99945cm
breadboards: 1

parts:
  R1 = Resistor [tolerance=±5% resistance=450 package=THT]
  VCC = Voltage Regulator - 5V [package="TO220 [THT]"]
  J4 = female pin header, 2 pins [form="♀ (female)"]
  J6 = female pin header, 2 pins [form="♀ (female)"]
  J5 = female pin header, 1 pin [form="♀ (female)"]
  R2 = Resistor [tolerance=±5% resistance=450 package=THT]
  VCC1 = Voltage Regulator - 5V [package="TO220 [THT]"]
  J7 = female pin header, 2 pins [form="♀ (female)"]
  J8 = female pin header, 2 pins [form="♀ (female)"]
  J9 = female pin header, 1 pin [form="♀ (female)"]
  Part1 = Arduino Uno (Rev3)
  S1 = H-Bridge with L298N
  S2 = H-Bridge with L298N
  M1 = DC Motor
  M2 = DC Motor
  M3 = DC Motor
  M4 = DC Motor
  Part2 = HC-05 [part_number=HC-05 package="breakout board"]
  VCC2 = Battery
  S4 = SPST Switch [package=switch-spdt_lock.007s]  # not connected

nets:
  GND: R1.Pin_0, VCC.GND, J4.pin2, S1.GND, S2.GND, Part2.GND, VCC2.-
  N1: R1.Pin_1, J6.pin2, J5.pin1, Part1.A4/SDA
  N2: VCC.output_voltage, J4.pin1, J6.pin1, VCC1.output_voltage, J7.pin1, J8.pin1, S1.5V
  N3: R2.Pin_0, VCC1.input_voltage, VCC1.GND, J8.pin2
  N4: R2.Pin_1, J7.pin2, J9.pin1, Part1.A5/SCL
  N5: Part1.D8, S2.IN1
  N6: Part1.D9_PWM, S2.IN2
  N7: Part1.D10_PWM/SS, S1.IN3
  N8: Part1.D11_PWM/MOSI, S1.IN4
  N9: Part1.D12/MISO, S1.IN1
  N10: Part1.D13/SCK, S1.IN2
  N11: Part1.D0/RX, Part2.TXD
  N12: Part1.D1/TX, Part2.RXD
  N13: Part1.D6_PWM, S2.IN4
  N14: Part1.D7, S2.IN3
  3V3: Part1.3V3, Part2.VCC
  VIN: Part1.VIN, S2.5V
  12V: S1.12V, S2.12V
  N15: S1.M1-01, M3.pin_2
  N16: S1.M1-02, M3.pin_1
  N17: S1.M2-01, M1.pin_2
  N18: S1.M2-02, M1.pin_1
  N19: S2.M1-01, M2.pin_2
  N20: S2.M1-02, M2.pin_1
  N21: S2.M2-01, M4.pin_2
  N22: S2.M2-02, M4.pin_1

custom parts:
  H-Bridge with L298N: h-bridge
  HC-05: A commonly available HC-05 Bluetooth breakout board.
