# Fritzing sketch pcb (saved by Fritzing 0.8.7b)
circuit board: 2.77362cm x 1.99945cm

parts:
  R1 = Resistor [tolerance=±5% resistance=450 package=THT]
  VCC = Voltage Regulator - 5V [package="TO220 [THT]"]
  J4 = female pin header, 2 pins [form="♀ (female)"]
  J6 = female pin header, 2 pins [form="♀ (female)"]
  J5 = female pin header, 1 pin [form="♀ (female)"]

nets:
  N1: R1.Pin_0, VCC.GND, J4.pin2
  N2: R1.Pin_1, J6.pin2, J5.pin1
  N3: VCC.output_voltage, J4.pin1, J6.pin1
